// Logisim project cpu_test.circ as structural Verilog: 4 circuits, main circuit main
module main (
  input  [15:0] Instruction,
  input  in_2,
  output [7:0] out_3
);

  wire [3:0] ControlRom_data;
  wire [7:0] registerfile_1_d1, registerfile_1_d2;

  ROM #(.addrWidth(4), .dataWidth(4)) ControlRom (.addr(Instruction[15:12]), .data(ControlRom_data));
  RegisterFile registerfile_1 (
    .Data(out_3), .Clock(in_2), .Enable(ControlRom_data[0]), .R1(Instruction[11:8]),
    .Write(Instruction[3:0]), .R2(Instruction[7:4]), .D1(registerfile_1_d1), .D2(registerfile_1_d2));
  ALU alu_1 (.A(registerfile_1_d1), .B(registerfile_1_d2), .SETTING(ControlRom_data[3:1]), .RESULT(out_3));

  // Notes on the sheet:
  //   contents of ControlRom (hex, n*v repeats v):
  //   0 0 1 3
endmodule

module ALU (
  input  [7:0] A,
  input  [7:0] B,
  input  [2:0] SETTING,
  output [7:0] RESULT
);

  wire [7:0] adder_1_out, and_1_out, nand_1_out, nor_1_out, or_1_out, subtractor_1_out, xnor_1_out, xor_1_out;

  Adder adder_1 (.a(A), .b(B), .out(adder_1_out));  // open: cin, cout
  Subtractor subtractor_1 (.a(A), .b(B), .out(subtractor_1_out));  // open: bin, bout
  assign and_1_out = A & B;  // AND_Gate and_1, 8 bits wide
  assign or_1_out = A | B;  // OR_Gate or_1, 8 bits wide
  assign xor_1_out = A ^ B;  // XOR_Gate xor_1, 8 bits wide
  assign nand_1_out = ~(A & B);  // NAND_Gate nand_1, 8 bits wide
  assign xnor_1_out = ~(A ^ B);  // XNOR_Gate xnor_1, 8 bits wide
  assign nor_1_out = ~(A | B);  // NOR_Gate nor_1, 8 bits wide
  Multiplexer #(.select(3), .width(8)) multiplexer_1 (
    .in0(adder_1_out), .in1(subtractor_1_out), .in2(and_1_out), .in3(or_1_out), .in4(xor_1_out),
    .in5(nand_1_out), .in6(xnor_1_out), .in7(nor_1_out), .out(RESULT), .sel(SETTING));

  // Notes on the sheet:
  //   B: initial=0x1
  //   A: initial=0x1
  //   Setting order is top to bottom from 0-7
endmodule

module RegisterFile (
  input  [7:0] Data,
  input  Clock,
  input  Enable,
  input  [3:0] R1,
  input  [3:0] Write,
  input  [3:0] R2,
  output [7:0] D1,
  output [7:0] D2
);

  wire demultiplexer_1_out1, demultiplexer_1_out2, demultiplexer_1_out3, demultiplexer_1_out4,
       demultiplexer_1_out5, demultiplexer_1_out6, demultiplexer_1_out7, demultiplexer_1_out8,
       demultiplexer_1_out9, demultiplexer_1_out10, demultiplexer_1_out11, demultiplexer_1_out12,
       demultiplexer_1_out13, demultiplexer_1_out14, demultiplexer_1_out15;
  wire [7:0] dualregister_1_out1, dualregister_1_out2, dualregister_2_out1, dualregister_2_out2,
       dualregister_3_out1, dualregister_3_out2, dualregister_4_out1, dualregister_4_out2,
       dualregister_5_out1, dualregister_5_out2, dualregister_6_out1, dualregister_6_out2,
       dualregister_7_out1, dualregister_7_out2, dualregister_8_out1, dualregister_8_out2,
       dualregister_9_out1, dualregister_9_out2, dualregister_10_out1, dualregister_10_out2,
       dualregister_11_out1, dualregister_11_out2, dualregister_12_out1, dualregister_12_out2,
       dualregister_13_out1, dualregister_13_out2, dualregister_14_out1, dualregister_14_out2,
       dualregister_15_out1, dualregister_15_out2;

  Demultiplexer #(.enable("true"), .select(4)) demultiplexer_1 (
    .out1(demultiplexer_1_out1), .out2(demultiplexer_1_out2), .out3(demultiplexer_1_out3),
    .out4(demultiplexer_1_out4), .out5(demultiplexer_1_out5), .out6(demultiplexer_1_out6),
    .out7(demultiplexer_1_out7), .out8(demultiplexer_1_out8), .out9(demultiplexer_1_out9),
    .out10(demultiplexer_1_out10), .out11(demultiplexer_1_out11), .out12(demultiplexer_1_out12),
    .out13(demultiplexer_1_out13), .out14(demultiplexer_1_out14), .out15(demultiplexer_1_out15), .in(Clock),
    .sel(Write), .en(Enable));  // open: out0
  DualRegister dualregister_1 (
    .Data(Data), .Clock(demultiplexer_1_out1), .OUT1(dualregister_1_out1), .OUT2(dualregister_1_out2));
  DualRegister dualregister_2 (
    .Data(Data), .Clock(demultiplexer_1_out2), .OUT1(dualregister_2_out1), .OUT2(dualregister_2_out2));
  DualRegister dualregister_3 (
    .Data(Data), .Clock(demultiplexer_1_out3), .OUT1(dualregister_3_out1), .OUT2(dualregister_3_out2));
  DualRegister dualregister_4 (
    .Data(Data), .Clock(demultiplexer_1_out4), .OUT1(dualregister_4_out1), .OUT2(dualregister_4_out2));
  DualRegister dualregister_5 (
    .Data(Data), .Clock(demultiplexer_1_out5), .OUT1(dualregister_5_out1), .OUT2(dualregister_5_out2));
  DualRegister dualregister_6 (
    .Data(Data), .Clock(demultiplexer_1_out6), .OUT1(dualregister_6_out1), .OUT2(dualregister_6_out2));
  DualRegister dualregister_7 (
    .Data(Data), .Clock(demultiplexer_1_out7), .OUT1(dualregister_7_out1), .OUT2(dualregister_7_out2));
  DualRegister dualregister_8 (
    .Data(Data), .Clock(demultiplexer_1_out8), .OUT1(dualregister_8_out1), .OUT2(dualregister_8_out2));
  DualRegister dualregister_9 (
    .Data(Data), .Clock(demultiplexer_1_out9), .OUT1(dualregister_9_out1), .OUT2(dualregister_9_out2));
  DualRegister dualregister_10 (
    .Data(Data), .Clock(demultiplexer_1_out10), .OUT1(dualregister_10_out1), .OUT2(dualregister_10_out2));
  DualRegister dualregister_11 (
    .Data(Data), .Clock(demultiplexer_1_out11), .OUT1(dualregister_11_out1), .OUT2(dualregister_11_out2));
  DualRegister dualregister_12 (
    .Data(Data), .Clock(demultiplexer_1_out12), .OUT1(dualregister_12_out1), .OUT2(dualregister_12_out2));
  DualRegister dualregister_13 (
    .Clock(demultiplexer_1_out13), .OUT1(dualregister_13_out1), .OUT2(dualregister_13_out2));  // open: Data
  DualRegister dualregister_14 (
    .Data(Data), .Clock(demultiplexer_1_out14), .OUT1(dualregister_14_out1), .OUT2(dualregister_14_out2));
  DualRegister dualregister_15 (
    .Data(Data), .Clock(demultiplexer_1_out15), .OUT1(dualregister_15_out1), .OUT2(dualregister_15_out2));
  Multiplexer #(.enable("true"), .select(4), .width(8)) multiplexer_1 (
    .in0({8{1'b0}}), .in1(dualregister_1_out2), .in2(dualregister_2_out2), .in3(dualregister_3_out2),
    .in4(dualregister_4_out2), .in5(dualregister_5_out2), .in6(dualregister_6_out2),
    .in7(dualregister_7_out2), .in8(dualregister_8_out2), .in9(dualregister_9_out2),
    .in10(dualregister_10_out2), .in11(dualregister_11_out2), .in12(dualregister_12_out2),
    .in13(dualregister_13_out2), .in14(dualregister_14_out2), .in15(dualregister_15_out2), .out(D2),
    .sel(R2), .en(Enable));
  Multiplexer #(.enable("true"), .select(4), .width(8)) multiplexer_2 (
    .in0({8{1'b0}}), .in1(dualregister_1_out1), .in2(dualregister_2_out1), .in3(dualregister_3_out1),
    .in4(dualregister_4_out1), .in5(dualregister_5_out1), .in6(dualregister_6_out1),
    .in7(dualregister_7_out1), .in8(dualregister_8_out1), .in9(dualregister_9_out1),
    .in10(dualregister_10_out1), .in11(dualregister_11_out1), .in12(dualregister_12_out1),
    .in13(dualregister_13_out1), .in14(dualregister_14_out1), .in15(dualregister_15_out1), .out(D1),
    .sel(R1), .en(Enable));
endmodule

module DualRegister (
  input  [7:0] Data,
  input  Clock,
  output [7:0] OUT1,
  output [7:0] OUT2
);

  Register register_1 (.D(Data), .clk(Clock), .Q(OUT1));  // open: en, clr
  Register register_2 (.D(Data), .clk(Clock), .Q(OUT2));  // open: en, clr
endmodule
